# Fritzing sketch Layout_slave_board_V2_comm (saved by Fritzing 0.9.3b)

parts:
  Part3 = Arduino Nano (Rev3.0)
  Part4 = Arduino Nano (Rev3.0)
  S1 = H-Bridge with L298N
  J42 = double row male pin header, 20 pins [form="♂ (male)"]
  J43 = double row male pin header, 20 pins [form="♂ (male)"]
  J44 = double row male pin header, 20 pins [form="♂ (male)"]
  J45 = shrouded pin header, 40 pins [form="♂ (shrouded male)"]  # not connected
  J1 = male pin header, 6 pins [form="♂ (male)"]
  J7 = male pin header, 2 pins [form="♂ (male)"]
  J6 = male pin header, 2 pins [form="♂ (male)"]
  J5 = male pin header, 2 pins [form="♂ (male)"]
  J4 = male pin header, 2 pins [form="♂ (male)"]
  Part5 = Arduino Nano (Rev3.0)
  Part6 = Arduino Nano (Rev3.0)
  J46 = male pin header, 6 pins [form="♂ (male)"]
  J47 = male pin header, 2 pins [form="♂ (male)"]
  J48 = male pin header, 2 pins [form="♂ (male)"]
  J49 = male pin header, 2 pins [form="♂ (male)"]
  J50 = male pin header, 2 pins [form="♂ (male)"]
  S2 = H-Bridge with L298N
  Part7 = Arduino Nano (Rev3.0)
  Part8 = Arduino Nano (Rev3.0)
  J51 = male pin header, 6 pins [form="♂ (male)"]
  J52 = male pin header, 2 pins [form="♂ (male)"]
  J53 = male pin header, 2 pins [form="♂ (male)"]
  J54 = male pin header, 2 pins [form="♂ (male)"]
  J55 = male pin header, 2 pins [form="♂ (male)"]
  S3 = H-Bridge with L298N
  J56 = shrouded pin header, 10 pins [form="♂ (shrouded male)"]
  J15 = shrouded pin header, 10 pins [form="♂ (shrouded male)"]
  J57 = male pin header, 1 pin [form="♂ (male)"]
  J58 = male pin header, 1 pin [form="♂ (male)"]
  D1 = Rectifier Diode [part_number=1N4001 package="300 mil [THT]"]
  D2 = Rectifier Diode [part_number=1N4001 package="300 mil [THT]"]
  D3 = Rectifier Diode [part_number=1N4001 package="300 mil [THT]"]
  D4 = Rectifier Diode [part_number=1N4001 package="300 mil [THT]"]
  J63 = male pin header, 1 pin [form="♂ (male)"]
  J64 = male pin header, 1 pin [form="♂ (male)"]
  J65 = male pin header, 1 pin [form="♂ (male)"]
  J66 = male pin header, 1 pin [form="♂ (male)"]
  R1 = Resistor [tolerance=±5% resistance=220 package=THT]
  J68 = male pin header, 1 pin [form="♂ (male)"]
  J69 = male pin header, 1 pin [form="♂ (male)"]
  D5 = Rectifier Diode [part_number=1N4001 package="300 mil [THT]"]
  J71 = male pin header, 1 pin [form="♂ (male)"]
  D6 = Rectifier Diode [part_number=1N4001 package="300 mil [THT]"]
  J74 = male pin header, 2 pins [form="♂ (male)"]
  J75 = male pin header, 2 pins [form="♂ (male)"]
  J76 = male pin header, 2 pins [form="♂ (male)"]
  J77 = male pin header, 2 pins [form="♂ (male)"]
  J78 = male pin header, 2 pins [form="♂ (male)"]
  J79 = male pin header, 2 pins [form="♂ (male)"]
  J80 = shrouded pin header, 6 pins [form="♂ (shrouded male)"]
  J81 = shrouded pin header, 6 pins [form="♂ (shrouded male)"]

nets:
  N1: Part3.D1/TX, D3.cathode
  N2: Part3.D0/RX, J76.pin1
  N3: Part3.D2, J42.pin6, J43.pin15, J7.pin1, J6.pin1
  N4: Part3.D3, J44.pin15, J7.pin2, J6.pin2
  N5: Part3.D4, S1.ENA, J1.pin1
  N6: Part3.D10, S1.IN2, J1.pin3
  N7: Part3.D11/MOSI, S1.IN1, J1.pin2
  N8: Part3.D12/MISO, J80.pin3
  N9: Part4.D1/TX, D4.cathode
  N10: Part4.D0/RX, J77.pin1
  N11: Part4.D2, J42.pin9, J43.pin12, J5.pin1, J4.pin1
  N12: Part4.D3, J44.pin12, J5.pin2, J4.pin2
  N13: Part4.D4, S1.ENB, J1.pin6
  N14: Part4.D10, S1.IN4, J1.pin5
  N15: Part4.D11/MOSI, S1.IN3, J1.pin4
  N16: Part4.D12/MISO, J80.pin2
  N17: Part4.5V, R1.Pin_0
  N18: S1.M1-01, J42.pin15, J43.pin6
  N19: S1.M1-02, J44.pin6
  N20: S1.M2-01, J44.pin3
  N21: S1.M2-02, J42.pin18, J43.pin3
  N22: J42.pin7, J43.pin14, J15.pin9
  N23: J42.pin8, J43.pin13, J15.pin10
  N24: J42.pin10, J43.pin11, Part6.D2, J47.pin1, J48.pin1
  N25: J42.pin11, J43.pin10, Part5.D2, J49.pin1, J50.pin1
  N26: J42.pin12, J42.pin13, J43.pin8, J43.pin9, J44.pin9, J58.pin1
  N27: J42.pin14, J43.pin7, J44.pin7, J44.pin8, J57.pin1
  N28: J42.pin16, J43.pin5, J15.pin7
  N29: J42.pin17, J43.pin4, J15.pin8
  N30: J42.pin19, J43.pin2, S2.M2-02
  N31: J42.pin20, J43.pin1, S2.M1-01
  N32: J44.pin1, S2.M1-02
  N33: J44.pin2, S2.M2-01
  N34: J44.pin4, J15.pin3
  N35: J44.pin5, J15.pin4
  N36: J44.pin10, Part5.D3, J49.pin2, J50.pin2
  N37: J44.pin11, Part6.D3, J47.pin2, J48.pin2
  N38: J44.pin13, J15.pin1
  N39: J44.pin14, J15.pin2
  N40: Part5.D1/TX, D1.cathode
  N41: Part5.D0/RX, J74.pin1
  N42: Part5.D4, J46.pin1, S2.ENA, S2.ENA-5V
  N43: Part5.D10, J46.pin3, S2.IN2
  N44: Part5.D11/MOSI, J46.pin2, S2.IN1
  N45: Part5.D12/MISO, J80.pin5
  N46: Part6.D1/TX, D2.cathode
  N47: Part6.D0/RX, J75.pin1
  N48: Part6.D4, J46.pin6, S2.ENB, S2.ENB-5V
  N49: Part6.D10, J46.pin5, S2.IN4
  N50: Part6.D11/MOSI, J46.pin4, S2.IN3
  N51: Part6.D12/MISO, J80.pin4
  N52: Part7.D1/TX, D6.cathode
  N53: Part7.D0/RX, J78.pin1
  N54: Part7.GND, Part7.D2, J54.pin1, J55.pin1, J56.pin2
  N55: Part7.D3, J54.pin2, J55.pin2, J56.pin9
  N56: Part7.D4, J51.pin1, S3.ENA, S3.ENA-5V
  N57: Part7.D9, Part7.D10, J51.pin3, S3.IN2
  N58: Part7.D11/MOSI, J51.pin2, S3.IN1
  N59: Part7.D12/MISO, J81.pin3
  N60: Part8.D0/RX, D5.cathode
  N61: Part8.RESET, J79.pin1
  N62: Part8.D2, J52.pin1, J53.pin1, J56.pin1
  N63: Part8.D3, J52.pin2, J53.pin2, J56.pin10
  N64: Part8.D4, J51.pin6, S3.ENB
  N65: Part8.D9, Part8.D10, J51.pin5, S3.IN4
  N66: Part8.D11/MOSI, J51.pin4, S3.IN3
  N67: Part8.D12/MISO, J81.pin2
  N68: S3.M1-01, J56.pin4
  N69: S3.M1-02, J56.pin7
  N70: S3.M2-01, J56.pin8
  N71: S3.M2-02, J56.pin3
  N72: D1.anode, D2.anode, D3.anode, D4.anode, J63.pin1, J64.pin1, J65.pin1, J66.pin1, R1.Pin_1, J68.pin1, J80.pin6
  N73: J69.pin1, D5.anode, J71.pin1, D6.anode, J81.pin6
  N74: J74.pin2, J75.pin2, J76.pin2, J77.pin2, J80.pin1
  N75: J78.pin2, J79.pin2, J81.pin1

notes:
  UAJ
  SKG
  SKF
  SKE
  Shoulder
  UAE
  Master

custom parts:
  H-Bridge with L298N: h-bridge
